# Fritzing sketch Sketch (saved by Fritzing 0.9.2b)
breadboards: 1

parts:
  GLCD_84x1 = Display84x48
  Componente1 = Arduino Pro Mini v13
  Power_plug1 = Power plug
  DS1 = DS18B20 1-Wire Temperature Sensor [part_number=DS18B20]
  Componente2 = Modulo Rele
  U2 = POT [package=pot_mammoth]

nets:
  GND: GLCD_84x1.connector12, Componente1.GND, Power_plug1.GND, DS1.GND, Componente2.A0, Componente2.pin_1, U2.S
  VCC: GLCD_84x1.connector14, Componente1.VCC, Power_plug1.VCC, DS1.VDD, U2.E
  N1: GLCD_84x1.connector15, Componente1.D5_PWM
  N2: GLCD_84x1.connector16, Componente1.D6_PWM
  N3: GLCD_84x1.connector17, Componente1.D7
  N4: GLCD_84x1.connector18, Componente1.D8
  N5: GLCD_84x1.connector19, Componente1.D9_PWM
  N6: Componente1.A0, U2.A
  N7: Componente1.D11_PWM/MOSI, Componente2.pin_2
  N8: Componente1.D3_PWM, DS1.DQ

custom parts:
  Modulo Rele: The Arduino Uno is a microcontroller board based on the ATmega328 (datasheet). It has 14 digital input/output pins (of which 6 can be used as PWM outputs), 6 analog inputs, a 16 MHz ceramic resonator, a USB connection, a power jack, an ICSP header, and a reset button. It contains everything needed to support the microcontroller; simply connect it to a computer with a USB cable or power it with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
